// Logisim project Norb_StdLib.circ as structural Verilog
module Norb_8B_Selector (
  input  [7:0] In8B,
  input  InSelect,
  output [7:0] OutResult
);

  and and_1 (OutResult[7], InSelect, In8B[7]);
  and and_2 (OutResult[6], InSelect, In8B[6]);
  and and_3 (OutResult[5], InSelect, In8B[5]);
  and and_4 (OutResult[4], InSelect, In8B[4]);
  and and_5 (OutResult[3], InSelect, In8B[3]);
  and and_6 (OutResult[2], InSelect, In8B[2]);
  and and_7 (OutResult[1], InSelect, In8B[1]);
  and and_8 (OutResult[0], InSelect, In8B[0]);
endmodule

module Norb_1T2_Decoder (
  input  In1B,
  output Out1,
  output Out0
);

  not not_1 (Out0, In1B);

  assign Out1 = In1B;
endmodule

module Norb_2T4_Decoder (
  input  [1:0] In2B,
  output Out3,
  output Out2,
  output Out1,
  output Out0
);

  wire norb_1t2_decoder_1_out0, norb_1t2_decoder_1_out1, norb_1t2_decoder_2_out0, norb_1t2_decoder_2_out1,
       not_1_out;

  Norb_1T2_Decoder norb_1t2_decoder_1 (.In1B(In2B[0]), .Out1(norb_1t2_decoder_1_out1), .Out0(norb_1t2_decoder_1_out0));
  Norb_1T2_Decoder norb_1t2_decoder_2 (.In1B(In2B[0]), .Out1(norb_1t2_decoder_2_out1), .Out0(norb_1t2_decoder_2_out0));
  and and_1 (Out3, In2B[1], norb_1t2_decoder_1_out1);
  and and_2 (Out2, norb_1t2_decoder_1_out0, In2B[1]);
  not not_1 (not_1_out, In2B[1]);
  and and_3 (Out1, not_1_out, norb_1t2_decoder_2_out1);
  and and_4 (Out0, norb_1t2_decoder_2_out0, not_1_out);
endmodule

module Norb_3T8_Decoder (
  input  [2:0] In3B,
  output Out4,
  output Out5,
  output Out6,
  output Out7,
  output Out0,
  output Out1,
  output Out2,
  output Out3
);

  wire norb_2t4_decoder_1_out0, norb_2t4_decoder_1_out1, norb_2t4_decoder_1_out2, norb_2t4_decoder_1_out3,
       norb_2t4_decoder_2_out0, norb_2t4_decoder_2_out1, norb_2t4_decoder_2_out2, norb_2t4_decoder_2_out3,
       not_1_out;

  Norb_2T4_Decoder norb_2t4_decoder_1 (
    .In2B(In3B[1:0]), .Out3(norb_2t4_decoder_1_out3), .Out2(norb_2t4_decoder_1_out2),
    .Out1(norb_2t4_decoder_1_out1), .Out0(norb_2t4_decoder_1_out0));
  Norb_2T4_Decoder norb_2t4_decoder_2 (
    .In2B(In3B[1:0]), .Out3(norb_2t4_decoder_2_out3), .Out2(norb_2t4_decoder_2_out2),
    .Out1(norb_2t4_decoder_2_out1), .Out0(norb_2t4_decoder_2_out0));
  and and_1 (Out4, In3B[2], norb_2t4_decoder_1_out0);
  and and_2 (Out5, In3B[2], norb_2t4_decoder_1_out1);
  not not_1 (not_1_out, In3B[2]);
  and and_3 (Out0, not_1_out, norb_2t4_decoder_2_out0);
  and and_4 (Out1, not_1_out, norb_2t4_decoder_2_out1);
  and and_5 (Out6, In3B[2], norb_2t4_decoder_1_out2);
  and and_6 (Out7, In3B[2], norb_2t4_decoder_1_out3);
  and and_7 (Out2, not_1_out, norb_2t4_decoder_2_out2);
  and and_8 (Out3, not_1_out, norb_2t4_decoder_2_out3);
endmodule

module Norb_8B_Matcher (
  input  [7:0] In8B_A,
  input  [7:0] In8B_B,
  output OutAEqB
);

  wire xor_1_out, xor_2_out, xor_3_out, xor_4_out, xor_5_out, xor_6_out, xor_7_out, xor_8_out;

  xor xor_1 (xor_1_out, In8B_A[7], In8B_B[7]);
  xor xor_2 (xor_2_out, In8B_A[6], In8B_B[6]);
  xor xor_3 (xor_3_out, In8B_A[5], In8B_B[5]);
  xor xor_4 (xor_4_out, In8B_A[4], In8B_B[4]);
  xor xor_5 (xor_5_out, In8B_A[3], In8B_B[3]);
  xor xor_6 (xor_6_out, In8B_A[2], In8B_B[2]);
  xor xor_7 (xor_7_out, In8B_A[1], In8B_B[1]);
  xor xor_8 (xor_8_out, In8B_A[0], In8B_B[0]);
  nor nor_1 (OutAEqB, xor_8_out, xor_7_out, xor_6_out, xor_5_out, xor_4_out, xor_3_out, xor_2_out, xor_1_out);
endmodule

module Norb_3B_Matcher (
  input  [2:0] In8B_A,
  input  [2:0] In8B_B,
  output OutAEqB
);

  wire xor_1_out, xor_2_out, xor_3_out;

  xor xor_1 (xor_1_out, In8B_A[2], In8B_B[2]);
  xor xor_2 (xor_2_out, In8B_A[1], In8B_B[1]);
  xor xor_3 (xor_3_out, In8B_A[0], In8B_B[0]);
  nor nor_1 (OutAEqB, xor_3_out, xor_2_out, xor_1_out);
endmodule

module Norb_7B_Matcher (
  input  [6:0] In8B_A,
  input  [6:0] In8B_B,
  output OutAEqB
);

  wire xor_1_out, xor_2_out, xor_3_out, xor_4_out, xor_5_out, xor_6_out, xor_7_out;

  xor xor_1 (xor_1_out, In8B_A[6], In8B_B[6]);
  xor xor_2 (xor_2_out, In8B_A[5], In8B_B[5]);
  xor xor_3 (xor_3_out, In8B_A[4], In8B_B[4]);
  xor xor_4 (xor_4_out, In8B_A[3], In8B_B[3]);
  xor xor_5 (xor_5_out, In8B_A[2], In8B_B[2]);
  xor xor_6 (xor_6_out, In8B_A[1], In8B_B[1]);
  xor xor_7 (xor_7_out, In8B_A[0], In8B_B[0]);
  nor nor_1 (OutAEqB, xor_7_out, xor_6_out, xor_5_out, xor_1_out, xor_4_out, xor_3_out, xor_2_out);
endmodule
